// Digital circuit 8bit_SAP_CPU.dig as structural Verilog
module _8bit_SAP_CPU (
  input  in_2,
  input  in_3,
  input  in_4,
  input  in_5,
  output [7:0] OUTPUT,
  output [7:0] CHECK,
  output [7:0] CHECK2
);

  wire C_P, CE, E_A, E_I, E_P, E_U, L_A, L_B, L_I, L_M, L_o, S_U;
  wire [3:0] Program_Counter_out, register_2_q;
  wire [7:0] add_sub_1_s, B_q, ramdualport_1_d, register_1_q;
  wire [7:4] register_2_q_2;

  Register #(.Bits(8)) register_1 (.D(CHECK), .C(in_4), .en(L_I), .Q(register_1_q));
  Counter #(.Bits(4)) Program_Counter (.en(C_P), .C(in_4), .clr(in_5), .out(Program_Counter_out));  // open: ovf
  Register #(.Bits(8)) register_2 (.D(CHECK), .C(in_4), .en(L_M), .Q({register_2_q_2, register_2_q}));
  RAMDualPort #(.AddrBits(4), .Bits(8)) ramdualport_1 (
    .A(register_2_q), .Din({8{1'b0}}), .str(in_2), .C(in_4), .ld(CE), .D(ramdualport_1_d));
  assign CHECK = CE ? ramdualport_1_d : 8'bz;  // Driver driver_1
  // Controller controller_1: pin names not known; wires that end beside it: L_o, L_B, E_U, S_U, E_A, L_A, E_I, L_I, CE, in_3, L_M, register_1_q[7:4], E_P, in_4, C_P
  PullDown #(.Bits(8)) pulldown_1 (.out(CHECK));
  assign CHECK = E_P ? {4'b0000, Program_Counter_out} : 8'bz;  // Driver driver_2
  assign CHECK = E_I ? {4'b0000, register_1_q[3:0]} : 8'bz;  // Driver driver_3
  Register #(.Bits(8)) A (.D(CHECK), .C(in_4), .en(L_A), .Q(CHECK2));
  assign CHECK = E_U ? add_sub_1_s : 8'bz;  // Driver driver_4
  Register #(.Bits(8)) B (.D(CHECK), .C(in_4), .en(L_B), .Q(B_q));
  Register #(.Bits(8)) u_Output (.D(CHECK), .C(in_4), .en(L_o), .Q(OUTPUT));
  add_sub add_sub_1 (.A(CHECK2), .B(B_q), .A_s(S_U), .S(add_sub_1_s));  // open: OV, TS, Cout
  assign CHECK = E_A ? CHECK2 : 8'bz;  // Driver driver_5

  // Other names for the same wires on the sheet: CLK = in_4; CLR = in_5; ENS = in_3; R_S = in_2
endmodule
